# Fritzing sketch PROJETO_V4 (saved by Fritzing 0.9.3b)
stripboards: 2

parts:
  M1 = DOIT Esp32 DevKit v1 (30 pins long, 11 pins width) [part_number=ESP32S-PIN30]  # not connected
  JACK2 = 2.1mm Barrel Jack with Terminal Block
  BAT1 = 12 battery [package=battery]
  MOD2 = Multi booster
  J3 = JST-VHR-3N [part_number=JST-VHR-3N package=THT]
  J6 = JST-VHR-3N [part_number=JST-VHR-3N package=THT]
  MOD3 = Multi booster
  J9 = Camdenboss CTB0158-5 [part_number=CTB0158-5 package=THT]
  J10 = Camdenboss CTB0158-5 [part_number=CTB0158-5 package=THT]
  J11 = Camdenboss CTB0158-5 [part_number=CTB0158-5 package=THT]
  J12 = Camdenboss CTB0158-5 [part_number=CTB0158-5 package=THT]
  J13 = Camdenboss CTB0158-5 [part_number=CTB0158-5 package=THT]
  J14 = Camdenboss CTB0158-5 [part_number=CTB0158-5 package=THT]
  J15 = Camdenboss CTB0158-5 [part_number=CTB0158-5 package=THT]
  J16 = Camdenboss CTB0158-5 [part_number=CTB0158-5 package=THT]
  J20 = Camdenboss CTB0158-2 [part_number=CTB0158-2 package=THT]
  J17 = Camdenboss CTB0158-5 [part_number=CTB0158-5 package=THT]
  J21 = Camdenboss CTB0158-2 [part_number=CTB0158-2 package=THT]  # not connected
  J18 = Camdenboss CTB0158-9 [part_number=CTB0158-9 package=THT]
  M2 = 1 chan 5v relay module
  VALVE1 = Plastic Solenoid Valve
  J22 = Camdenboss CTB0158-5 [part_number=CTB0158-5 package=THT]
  J23 = Camdenboss CTB0158-5 [part_number=CTB0158-5 package=THT]
  VALVE2 = Plastic Solenoid Valve
  M4 = 1 chan 5v relay module
  Q6 = NPN-Transistor [package="TO92 [THT]"]
  Q7 = NPN-Transistor [package="TO92 [THT]"]
  R14 = Resistor [tolerance=±5% resistance=10k package=THT]
  R15 = Resistor [tolerance=±5% resistance=10k package=THT]
  DHT2 = DHT11 Humitidy and Temperature Sensor (3 pins)
  Componente2 = LCD1602-I2C
  e-radionica_com1 = LM393 LDR breakout [part_number=100027]
  J24 = Camdenboss CTB0158-5 [part_number=CTB0158-5 package=THT]
  J25 = Camdenboss CTB0158-5 [part_number=CTB0158-5 package=THT]
  Componente25 = Analog Digital MUX Breakout
  J19 = Camdenboss CTB0158-8 [part_number=CTB0158-8 package=THT]  # not connected
  Componente26 = FC-28 Soil Hygrometer Module - Probe
  Componente27 = FC-28 Soil Hygrometer Module
  Componente28 = FC-28 Soil Hygrometer Module
  J26 = Camdenboss CTB0158-3 [part_number=CTB0158-3 package=THT]
  J27 = Camdenboss CTB0158-3 [part_number=CTB0158-3 package=THT]
  J28 = Camdenboss CTB0158-5 [part_number=CTB0158-5 package=THT]
  J29 = Camdenboss CTB0158-5 [part_number=CTB0158-5 package=THT]
  J30 = Camdenboss CTB0158-5 [part_number=CTB0158-5 package=THT]
  J31 = Camdenboss CTB0158-5 [part_number=CTB0158-5 package=THT]
  J32 = Camdenboss CTB0158-5 [part_number=CTB0158-5 package=THT]
  J33 = Camdenboss CTB0158-5 [part_number=CTB0158-5 package=THT]
  J34 = Camdenboss CTB0158-5 [part_number=CTB0158-5 package=THT]
  J35 = Camdenboss CTB0158-5 [part_number=CTB0158-5 package=THT]
  Componente29 = FC-28 Soil Hygrometer Module
  Componente30 = FC-28 Soil Hygrometer Module
  Componente32 = FC-28 Soil Hygrometer Module - Probe
  Componente34 = FC-28 Soil Hygrometer Module - Probe
  Componente35 = FC-28 Soil Hygrometer Module - Probe
  Capacitive_Soil_Moisture_Sensor1 = DFRobot Capacitive Soil Moisture Sensor V1.0 [part_number=SEN0193]
  Capacitive_Soil_Moisture_Sensor2 = DFRobot Capacitive Soil Moisture Sensor V1.0 [part_number=SEN0193]
  Part3 = Solar Panel [package="Renogy 50 Watts 12 Volt Monocrystalline Bendable Solar Panel"]
  Part4 = Solar Charge Controller [part_number="HGX Series Solar Charge Controller PWM" package=PWM-Model]
  U1 = M40 [package=1x40_offset]  # not connected
  U2 = M40 [package=1x40_offset]  # not connected

nets:
  N1: JACK2.POS, J22.terminal_2
  N2: JACK2.NEG, J20.pin2, J20.terminal_2, J23.terminal_2
  N3: BAT1.-, Part4.Connector_4
  N4: BAT1.+, Part4.Connector_3
  N5: MOD2.BAT+, J6.pin_5
  N6: MOD2.BAT-, MOD2.GND, MOD2.Jumper_A, MOD2.Jumper_B, J3.pin_5, J23.terminal_1
  N7: MOD2.V+, J22.terminal_1
  N8: J3.pin_4, Part4.Connector_6
  N9: J3.pin_6, MOD3.BAT-, MOD3.GND, MOD3.Jumper_A, J27.terminal_1
  N10: J6.pin_4, Part4.Connector_5
  N11: J6.pin_6, MOD3.BAT+
  N12: MOD3.V+, J26.terminal_3
  N13: J9.terminal_1, J26.terminal_1
  N14: J9.terminal_2, Componente25.VCC
  N15: J9.terminal_4, e-radionica_com1.VCC
  N16: J9.terminal_5, J12.terminal_1
  N17: J10.terminal_1, J27.terminal_3
  N18: J10.terminal_2, Componente25.EN
  N19: J10.terminal_3, Componente25.GND
  N20: J10.terminal_4, e-radionica_com1.GND
  N21: J10.terminal_5, J11.terminal_1
  N22: J11.terminal_2, Componente2.GND
  N23: J11.terminal_3, DHT2.Gnd
  N24: J11.terminal_4, J18.terminal_7, M4.pin_3, Q6.E, Q6.B, Q6.C, R14.Pin_0, R14.Pin_1
  N25: J11.terminal_5, J13.terminal_1
  N26: J12.terminal_2, Componente2.VCC
  N27: J12.terminal_5, J14.terminal_1
  N28: J13.terminal_2, J18.terminal_9, M2.pin_3, Q7.E, Q7.B, Q7.C, R15.Pin_0, R15.Pin_1
  N29: J13.terminal_5, J29.terminal_1
  N30: J14.terminal_2, DHT2.Plus
  N31: J14.terminal_3, M2.pin_1
  N32: J14.terminal_4, M4.pin_1
  N33: J14.terminal_5, J28.terminal_1
  N34: J15.terminal_4, Componente25.SIG
  N35: J15.terminal_5, Componente25.S3
  N36: J16.pin2, J16.terminal_2, Componente25.S1
  N37: J16.pin3, J16.terminal_3, Componente25.S0
  N38: J16.terminal_1, Componente25.S2
  N39: J20.pin1, J20.terminal_1
  N40: J17.terminal_1, DHT2.Signal
  N41: J17.terminal_2, e-radionica_com1.AO
  N42: J17.terminal_4, Componente2.SCL
  N43: J18.terminal_8, Componente2.SDA
  N44: M2.pin_4, VALVE1.no_name_yet#1
  N45: M2.pin_5, J22.terminal_4
  N46: VALVE1.no_name_yet#2, J23.terminal_4
  N47: J22.terminal_3, M4.pin_5
  N48: J22.terminal_5, J24.terminal_1
  N49: J23.terminal_3, VALVE2.no_name_yet#2
  N50: J23.terminal_5, J25.terminal_1
  N51: VALVE2.no_name_yet#1, M4.pin_4
  N52: Componente25.C0, Componente30.AO
  N53: Componente25.C1, Componente29.AO
  N54: Componente25.C2, Componente28.AO
  N55: Componente25.C3, Componente27.AO
  N56: Componente25.C4, Capacitive_Soil_Moisture_Sensor1.A
  N57: Componente25.C5, Capacitive_Soil_Moisture_Sensor2.A
  N58: Componente26.POS, Componente27.POS
  N59: Componente26.NEG, Componente27.NEG
  N60: Componente27.VCC, J32.terminal_4
  N61: Componente27.GND, J34.terminal_2
  N62: Componente28.VCC, J31.terminal_2
  N63: Componente28.GND, J30.terminal_4
  N64: Componente28.POS, Componente32.POS
  N65: Componente28.NEG, Componente32.NEG
  N66: J26.terminal_2, J31.terminal_5
  N67: J27.terminal_2, J30.terminal_1
  N68: J30.terminal_2, Componente30.GND
  N69: J30.terminal_3, Componente29.GND
  N70: J30.terminal_5, J34.terminal_1
  N71: J31.terminal_1, J32.terminal_5
  N72: J31.terminal_3, Componente29.VCC
  N73: J31.terminal_4, Componente30.VCC
  N74: J32.terminal_1, J33.terminal_5
  N75: J32.terminal_3, Capacitive_Soil_Moisture_Sensor1.VCC
  N76: J34.terminal_3, Capacitive_Soil_Moisture_Sensor1.GND
  N77: J34.terminal_4, Capacitive_Soil_Moisture_Sensor2.GND
  N78: J34.terminal_5, J35.terminal_1
  N79: Componente29.POS, Componente34.POS
  N80: Componente29.NEG, Componente34.NEG
  N81: Componente30.POS, Componente35.POS
  N82: Componente30.NEG, Componente35.NEG
  N83: Part3.Connector_1, Part4.Connector_1
  N84: Part3.Connector_2, Part4.Connector_2

notes:
  Entrada 12v
  REGULADOR DE TENSAO LM2596
  Bateria de 12V / 7Ah a 20Ah
  Controlador de carga solar PWM (Pulse Width Modulation).
  Tensão de trabalho: 12V de 50W de potencia
  CONVERSOR DC-DC STEP DOWN
  CONVERTER DE 12V PARA 5V
  ESTABILIZAR PARA 12V
  D03 D21 D19 D18 D05 D17 D16 D04 D02
  P7 P6 P5 P4 P3 P2 P1 P0
  D39 D34 D35 D32 D33 D25 D26 D27 D14 D12 D13 D15 D23 D22 D01
  5V GND
  SAÍDA
  Transistor BC547
  Resistor de 10KΩ
  Placa fenolite perfurada
  conectores de derivação wago 221
  Todos esses verdinhos são:
  Todos esses brancos são:
  MULTIPLEXADOR CD74HC4067
  margem
  Anexo II
  58
  Sobre essa componentes verdes ao redor da Esp32
  Eles são a representação do Esp32 Base Board, uma placa expansora que eu não achei para adicionar na prototipagem, então para simular, eu coloquei esses quadrinhos verdes, nde vão os fios parafusaveis.

custom parts:
  DOIT Esp32 DevKit v1 (30 pins long, 11 pins width): The DOIT Esp32 DevKit v1 is one of the development board created by DOIT to evaluate the ESP-WROOM-32 module. It is based on the ESP32 microcontroller that boasts Wifi, Bluetooth, Ethernet and Low Power support all in a single chip. (vanepp) made breadboard work, adjusted pin numbering and labels and reduced size of schematic and cleaned up pcb. This chip is 30pins long (2 x15) and 11 pins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
  12 battery: 12V lead acid type battery, like the Husqvarna YTH2448 12V 35AH battery. This is the mini version 1/4 the size of the actual battery to be closer to typical breadboard parts (around 2in wide rathher than 7in). The pads in pcb are sized to accomidate up to 14ga wire (as these batterys will deliver high currents.)
  Multi booster: Input voltage range: 2.5V + Current: 1A Boost output voltage: 5V/ 8V/ 9V 12V ------------ A B VOUT ------------ 0 0 5V 0 1 8V 1 0 9V 1 1 12V ------------
  1 chan 5v relay module: 1 Channel 5V Relay Module Board Shield with Optocoupler Support High and Low Level Trigger for Arduino.
  DHT11 Humitidy and Temperature Sensor (3 pins): DHT11 Humidity and Temperature Sensor (3 pins).
  LCD1602-I2C: A standard character display, usually with 2x16 characters. Comes in many colors with LCM1602 IIC attached.
  FC-28 Soil Hygrometer Module - Probe: The FC-28 is a soil hygrometer module that uses the Texas Instruments LM393 comparator chip to provide an analog measurement of soil humidity.
  FC-28 Soil Hygrometer Module: The FC-28 is a soil hygrometer module that uses the Texas Instruments LM393 comparator chip to provide an analog measurement of soil humidity. The digital output is high when soil moisture is over a certain threshold, as determined by adjusting the potentiometer.
  DFRobot Capacitive Soil Moisture Sensor V1.0: DFRobot Capacitive Soil Moisture Sensor V1.0 This product measures soil moisture levels by capacitive sensing, rather than resistive sensing like other types of moisture sensor. It is made of a corrosion resistant material giving it a long service life. Insert it into soil and impress your friends with the real-time soil moisture data! The product includes an on-board voltage regulator which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
  Solar Panel: Renogy 50 Watts 12 Volt Solar Panel
  Solar Charge Controller: PWM-Solar Charge Controller
